# Fritzing sketch main (saved by Fritzing 0.9.6b)
breadboards: 1

parts:
  U1 = 7-SEGMENT-DISPLAY [package=7-segment-display]
  R1 = Resistor [tolerance=±5% power=0.25 resistance=220 package=THT]
  R2 = Resistor [tolerance=±5% power=0.25 resistance=220 package=THT]
  R3 = Resistor [tolerance=±5% power=0.25 resistance=220 package=THT]
  R4 = Resistor [tolerance=±5% power=0.25 resistance=220 package=THT]
  R5 = Resistor [tolerance=±5% power=0.25 resistance=220 package=THT]
  R6 = Resistor [tolerance=±5% power=0.25 resistance=220 package=THT]
  R7 = Resistor [tolerance=±5% power=0.25 resistance=220 package=THT]
  PIC_16F877A1 = PIC 16F877A [package=THT]

nets:
  N1: U1.E, R7.Pin_1
  N2: U1.D, R5.Pin_1
  N3: U1.G1, R4.Pin_1
  N4: U1.C, PIC_16F877A1.VSS#30
  N5: U1.DP, R3.Pin_1
  N6: U1.A, R2.Pin_1
  N7: U1.G2, R1.Pin_1
  N8: U1.G, R6.Pin_1
  N9: R1.Pin_0, PIC_16F877A1.RB7
  N10: R2.Pin_0, PIC_16F877A1.RB6
  N11: R3.Pin_0, PIC_16F877A1.RB5
  N12: R4.Pin_0, PIC_16F877A1.RB4
  N13: R5.Pin_0, PIC_16F877A1.RB3
  N14: R6.Pin_0, PIC_16F877A1.RB2
  N15: R7.Pin_0, PIC_16F877A1.RB1
